# Fritzing sketch Test Screw Terminal Breakout (saved by Fritzing 0.9.4)
circuit board: 8cm x 4cm

parts:
  J6 = screw terminal, 20 pins
  J7 = screw terminal, 20 pins
  1 = shrouded pin header, 40 pins [form="♂ (shrouded male)"]

nets:
  INJ-1-OUT: J6.pin1, J7.pin20, 1.pin1, 1.pin40
  INJ-2-OUT: J6.pin2, J7.pin19, 1.pin2, 1.pin39
  INJ-3-OUT: J6.pin3, J6.pin4, 1.pin3, 1.pin4
  INJ-4-OUT: J6.pin5, J6.pin6, 1.pin5, 1.pin6
  IGN-1-OUT: J6.pin7, 1.pin7
  IGN-4-OUT: J6.pin8, 1.pin8
  GND: J6.pin9, J6.pin10, J6.pin12, J7.pin3, 1.pin9, 1.pin10, 1.pin12, 1.pin23
  MAP-CPU-A3: J6.pin11, 1.pin11
  5V: J6.pin13, J7.pin8, 1.pin13, 1.pin28
  LC-1-OUT: J6.pin14, 1.pin14
  LC-2-OUT: J6.pin15, 1.pin15
  LC-3-OUT: J6.pin16, 1.pin16
  LC-4-OUT: J6.pin17, 1.pin17
  LC-5-OUT: J6.pin18, 1.pin18
  CLT Sensor: J6.pin19, 1.pin19
  IAT Sensor: J6.pin20, 1.pin20
  O2 Sensor: J7.pin1, 1.pin21
  TPS Sensor: J7.pin2, 1.pin22
  VR2+: J7.pin4, 1.pin24
  VR1+: J7.pin5, 1.pin25
  VR2-: J7.pin6, 1.pin26
  VR1-: J7.pin7, 1.pin27
  STEP-2B-OUT: J7.pin9, 1.pin29
  STEP-2A-OUT: J7.pin10, 1.pin30
  STEP-1A-OUT: J7.pin11, 1.pin31
  STEP-1B-OUT: J7.pin12, 1.pin32
  IGN-3-OUT: J7.pin13, 1.pin33
  IGN-2-OUT: J7.pin14, 1.pin34
  BOOST-OUT: J7.pin15, 1.pin35
  HC-1-OUT: J7.pin16, 1.pin36
  IDLE-OUT: J7.pin17, 1.pin37
  HC-2-OUT: J7.pin18, 1.pin38

notes:
  inj1
  Aaron S. 2020
  DetonationEMS.com
  20
  21
  40
  1
  CLT IAT
  PRT2 PRT3 PRT4 PRT5
  IGN1 IGN4 MAP PRT1
  INJ1 ING2 INJ3 INJ4
  BOOST ID2 PWM VVT
  IGN3 IGN2
  VR2+ VR1+ VR2- VR1-
  ID2B ID2A ID1A ID1B
  Mount IDC to Bottom
