# Fritzing sketch Universal v1.2 (saved by Fritzing 0.9.4)
circuit board: 7.5cm x 2.5cm

parts:
  1 = shrouded pin header, 40 pins [form="♂ (shrouded male)"]
  J4 = female pin header, 20 pins [form="♀ (female)"]
  J5 = female pin header, 20 pins [form="♀ (female)"]
  12v_GND = screw terminal, 2 pins
  GND_12v = screw terminal, 2 pins

nets:
  INJ-1-OUT: 1.pin1, 1.pin40, J4.pin20, J5.pin20
  INJ-2-OUT: 1.pin2, 1.pin39, J4.pin19, J5.pin19
  INJ-3-OUT: 1.pin3, 1.pin4, J4.pin17, J4.pin18
  INJ-4-OUT: 1.pin5, 1.pin6, J4.pin15, J4.pin16
  IGN-1-OUT: 1.pin7, J4.pin14
  IGN-4-OUT: 1.pin8, J4.pin13
  GND: 1.pin9, 1.pin10, 1.pin12, 1.pin23, J4.pin9, J4.pin11, J4.pin12, J5.pin3, 12v_GND.pin1, GND_12v.pin1
  MAP-CPU-A3: 1.pin11, J4.pin10
  5V: 1.pin13, 1.pin28, J4.pin8, J5.pin8
  LC-1-OUT: 1.pin14, J4.pin7
  LC-2-OUT: 1.pin15, J4.pin6
  LC-3-OUT: 1.pin16, J4.pin5
  LC-4-OUT: 1.pin17, J4.pin4
  LC-5-OUT: 1.pin18, J4.pin3
  CLT Sensor: 1.pin19, J4.pin2
  IAT Sensor: 1.pin20, J4.pin1
  O2 Sensor: 1.pin21, J5.pin1
  TPS Sensor: 1.pin22, J5.pin2
  VR2+: 1.pin24, J5.pin4
  VR1+: 1.pin25, J5.pin5
  VR2-: 1.pin26, J5.pin6
  VR1-: 1.pin27, J5.pin7
  STEP-2B-OUT: 1.pin29, J5.pin9
  STEP-2A-OUT: 1.pin30, J5.pin10
  STEP-1A-OUT: 1.pin31, J5.pin11
  STEP-1B-OUT: 1.pin32, J5.pin12
  IGN-3-OUT: 1.pin33, J5.pin13
  IGN-2-OUT: 1.pin34, J5.pin14
  BOOST-OUT: 1.pin35, J5.pin15
  HC-1-OUT: 1.pin36, J5.pin16
  IDLE-OUT: 1.pin37, J5.pin17
  HC-2-OUT: 1.pin38, J5.pin18
  12V-raw: 12v_GND.pin2, GND_12v.pin2

notes:
  Speeduino v0.4, Connector 1
  inj1
  Aaron S. 2020
  DetonationEMS.com
  20
  21
  40
  1
  CLT IAT
  PRT2 PRT3 PRT4 PRT5
  IGN1 IGN4 MAP PRT1
  INJ1 ING2 INJ3 INJ4
  BOOST ID2 PWM VVT
  IGN3 IGN2
  VR2+ VR1+ VR2- VR1-
  ID2B ID2A ID1A ID1B
