# Fritzing sketch v1.3 (saved by Fritzing 0.9.4)
circuit board: 10cm x 10cm

parts:
  Arduino_Mega_2560 = Arduino Mega 2560 (Rev3) [part_number="Arduino Mega 2560"]
  Q1 = Basic FET N-Channel [part_number=STP62NS04Z package="TO220 [THT]"]
  Q2 = Basic FET N-Channel [part_number=STP62NS04Z package="TO220 [THT]"]
  Q3 = Basic FET N-Channel [part_number=STP62NS04Z package="TO220 [THT]"]
  Q4 = Basic FET N-Channel [part_number=STP62NS04Z package="TO220 [THT]"]
  U2 = V18ZA2P [part_number=ERZV14D220 package=v18za2p]
  IC3 = IC, DIP package, 8 pins [chip_label="Dual VR Conditioner"]
  JP1 = female pin header, 3 pins [form="♀ (female)"]
  JP2 = female pin header, 3 pins [form="♀ (female)"]
  JP3 = female pin header, 3 pins [form="♀ (female)"]
  JP4 = female pin header, 2 pins [form="♀ (female)"]
  JP5 = female pin header, 2 pins [form="♀ (female)"]
  Q5 = Basic FET N-Channel [part_number=STP62NS04Z package="TO220 [THT]"]
  Q7 = Basic FET N-Channel [part_number=STP62NS04Z package="TO220 [THT]"]
  Q6 = Basic FET N-Channel [part_number=STP62NS04Z package="TO220 [THT]"]
  Q8 = Basic FET N-Channel [part_number=STP62NS04Z package="TO220 [THT]"]
  J143 = female pin header, 1 pin [form="♀ (female)"]  # not connected
  J144 = female pin header, 1 pin [form="♀ (female)"]  # not connected
  C15 = Ceramic Capacitor [capacitance=0.1µF voltage=50V package="0805 [SMD, multilayer]"]
  C13 = Ceramic Capacitor [capacitance=0.1µF voltage=50V package="0805 [SMD, multilayer]"]
  J169 = female pin header, 1 pin [form="♀ (female)"]  # not connected
  J170 = female pin header, 1 pin [form="♀ (female)"]  # not connected
  J172 = female pin header, 1 pin [form="♀ (female)"]  # not connected
  J173 = female pin header, 1 pin [form="♀ (female)"]  # not connected
  J174 = female pin header, 1 pin [form="♀ (female)"]  # not connected
  J176 = female pin header, 1 pin [form="♀ (female)"]  # not connected
  J177 = female pin header, 1 pin [form="♀ (female)"]  # not connected
  J180 = female pin header, 1 pin [form="♀ (female)"]  # not connected
  J182 = female pin header, 1 pin [form="♀ (female)"]  # not connected
  J186 = female pin header, 1 pin [form="♀ (female)"]  # not connected
  IC6 = ULN2003A [package="SO16 [SMD]"]
  C16 = Tantalum Capacitor [capacitance=10µF voltage=35V package="A 3216 [SMD, tantalum]"]
  J4 = shrouded pin header, 40 pins [form="♂ (shrouded male)"]
  J3 = screw terminal, 2 pins
  IC1 = SO08-EIAJ [chip_label=IC package=SO]
  IC2 = SO08-EIAJ [chip_label=IC part_number=" C44150" package=SO]
  J210 = female pin header, 1 pin [form="♀ (female)"]  # not connected
  J211 = female pin header, 1 pin [form="♀ (female)"]  # not connected
  J213 = female pin header, 1 pin [form="♀ (female)"]  # not connected
  J215 = female pin header, 1 pin [form="♀ (female)"]  # not connected
  MAP = SO08w [chip_label=IC package=SO(w)]
  D15 = Diode [part_number=us1m package=sma-diode]
  DRV8825 = DRV 8825 Stepper Motor Carrier, High Current [part_number="DRV 8825"]
  C14 = Tantalum Capacitor [capacitance=47µF voltage=10V package="A 3216 [SMD, tantalum]"]
  J216 = female pin header, 1 pin [form="♀ (female)"]  # not connected
  J217 = female pin header, 1 pin [form="♀ (female)"]  # not connected
  J218 = female pin header, 1 pin [form="♀ (female)"]  # not connected
  J219 = female pin header, 1 pin [form="♀ (female)"]  # not connected
  J220 = female pin header, 1 pin [form="♀ (female)"]  # not connected
  J221 = female pin header, 1 pin [form="♀ (female)"]  # not connected
  J222 = female pin header, 1 pin [form="♀ (female)"]  # not connected
  J223 = female pin header, 1 pin [form="♀ (female)"]  # not connected
  J224 = female pin header, 1 pin [form="♀ (female)"]  # not connected
  J109 = female pin header, 5 pins [form="♀ (female)"]
  J110 = female pin header, 5 pins [form="♀ (female)"]
  U1 = Voltage Regulator - 5V [part_number=C85225 package="DPak [SMD]"]
  R66 = Resistor [tolerance=±5% resistance=2.2 power=2W package="0603 [SMD]"]
  LED1 = smd LED [color="Red (633nm)" package="0603 [SMD]"]
  R69 = Resistor [tolerance=±5% resistance=2.2 power=2W package="0603 [SMD]"]
  R68 = Resistor [tolerance=±5% resistance=2.2 power=2W package="0603 [SMD]"]
  R67 = Resistor [tolerance=±5% resistance=2.2 power=2W package="0603 [SMD]"]
  LED2 = smd LED [color="Red (633nm)" package="0603 [SMD]"]
  LED3 = smd LED [color="Red (633nm)" package="0603 [SMD]"]
  LED4 = smd LED [color="Red (633nm)" package="0603 [SMD]"]
  AUX_(1_3) = shrouded pin header, 8 pins [form="♂ (shrouded male)"]
  R1 = Resistor [tolerance=±5% resistance=220 power=0.25 package=THT]
  R3 = Resistor [tolerance=±5% resistance=220 power=0.25 package=THT]
  R29 = Resistor [tolerance=±5% resistance=1k package="0603 [SMD]"]
  R24 = Resistor [tolerance=±5% resistance=1k package="0603 [SMD]"]
  R35 = Resistor [tolerance=±5% resistance=100k package="0603 [SMD]"]
  R23 = Resistor [tolerance=±5% resistance=1k package="0603 [SMD]"]
  R37 = Resistor [tolerance=±5% resistance=100k package="0603 [SMD]"]
  R36 = Resistor [tolerance=±5% resistance=100k package="0603 [SMD]"]
  R30 = Resistor [tolerance=±5% resistance=1k package="0603 [SMD]"]
  R38 = Resistor [tolerance=±5% resistance=100k package="0603 [SMD]"]
  R21 = Resistor [tolerance=±5% resistance=1k package="0603 [SMD]"]
  C7 = Ceramic Capacitor [capacitance=0.1µF package="0603 [SMD, multilayer]"]
  R8 = Resistor [tolerance=±5% resistance=470 package="0603 [SMD]"]
  R60 = Resistor [tolerance=±1% resistance=220 package="0603 [SMD]"]
  R59 = Resistor [tolerance=±5% resistance=220 package="0603 [SMD]"]
  R39 = Resistor [tolerance=±1% resistance=1k package="0603 [SMD]"]
  R40 = Resistor [tolerance=±1% resistance=1k package="0603 [SMD]"]
  R62 = Resistor [tolerance=±5% resistance=120 package="0603 [SMD]"]
  R75 = Resistor [tolerance=±5% resistance=1k package="0603 [SMD]"]
  R79 = Resistor [tolerance=±5% resistance=470 package="0603 [SMD]"]
  R7 = Resistor [tolerance=±0.1% resistance=3.9k package="0603 [SMD]"]
  R51 = Resistor [tolerance=±5% resistance=1k package="0603 [SMD]"]
  R57 = Resistor [tolerance=±5% resistance=1k package="0603 [SMD]"]
  R50 = Resistor [tolerance=±5% resistance=1k package="0603 [SMD]"]
  R58 = Resistor [tolerance=±5% resistance=1k package="0603 [SMD]"]
  R49 = Resistor [tolerance=±5% resistance=100k power=0.25W package="0603 [SMD]"]
  R55 = Resistor [tolerance=±5% resistance=100k package="0603 [SMD]"]
  R48 = Resistor [tolerance=±5% resistance=100k package="0603 [SMD]"]
  R56 = Resistor [tolerance=±5% resistance=100k power=0.25W package="0603 [SMD]"]
  R61 = Resistor [tolerance=±5% resistance=2.49k package="0603 [SMD]"]
  C1 = Ceramic Capacitor [capacitance=0.1µF package="0603 [SMD, multilayer]"]
  C3 = Ceramic Capacitor [capacitance=0.1µF package="0603 [SMD, multilayer]"]
  C5 = Ceramic Capacitor [capacitance=0.1µF package="0603 [SMD, multilayer]"]
  C9 = Ceramic Capacitor [capacitance=0.1µF package="0603 [SMD, multilayer]"]
  C2 = Ceramic Capacitor [capacitance=0.22µF package="0603 [SMD, multilayer]"]
  C4 = Ceramic Capacitor [capacitance=0.22µF package="0603 [SMD, multilayer]"]
  C6 = Ceramic Capacitor [capacitance=0.22µF package="0603 [SMD, multilayer]"]
  C10 = Ceramic Capacitor [capacitance=0.22µF package="0603 [SMD, multilayer]"]
  C8 = Ceramic Capacitor [capacitance=0.22µF package="0603 [SMD, multilayer]"]
  C24 = Ceramic Capacitor [capacitance=100nF package="0603 [SMD, multilayer]"]
  C27 = Ceramic Capacitor [capacitance="100 nF" package="0603 [SMD, multilayer]"]
  C29 = Ceramic Capacitor [capacitance="100 nF" package="0603 [SMD, multilayer]"]
  C26 = Ceramic Capacitor [capacitance="100 nF" package="0603 [SMD, multilayer]"]
  C28 = Ceramic Capacitor [capacitance="100 nF" package="0603 [SMD, multilayer]"]
  C25 = Ceramic Capacitor [capacitance=0.01µF package="0603 [SMD, multilayer]"]
  R2 = Resistor [tolerance=±5% resistance=470 package="0603 [SMD]"]
  R4 = Resistor [tolerance=±5% resistance=470 package="0603 [SMD]"]
  R6 = Resistor [tolerance=±5% resistance=470 package="0603 [SMD]"]
  R22 = Resistor [tolerance=±5% resistance=470 package="0603 [SMD]"]
  R65 = Resistor [tolerance=±5% resistance=220 package="0603 [SMD]"]
  R64 = Resistor [tolerance=±5% resistance=220 package="0603 [SMD]"]
  R41 = Resistor [tolerance=±5% resistance=470 package="0603 [SMD]"]
  C20 = Ceramic Capacitor [capacitance=1µF voltage=35V package="0603 [SMD, multilayer]"]
  C12 = Ceramic Capacitor [capacitance=1µF voltage=35V package="0603 [SMD, multilayer]"]
  C11 = Ceramic Capacitor [capacitance=1µF voltage=35V package="0603 [SMD, multilayer]"]
  C19 = Ceramic Capacitor [capacitance=0.01µF voltage=35V package="0603 [SMD, multilayer]"]
  C18 = Ceramic Capacitor [capacitance=1pF voltage=35V package="0603 [SMD, multilayer]"]
  C31 = Ceramic Capacitor [capacitance=4.7µ package="0603 [SMD, multilayer]"]
  R76 = Resistor [tolerance=±5% resistance=51k package="0603 [SMD]"]
  R13 = Resistor [tolerance=±5% resistance=100k package="0603 [SMD]"]
  R12 = Resistor [tolerance=±5% resistance=1k power=0.25W package="0603 [SMD]"]
  R10 = Resistor [tolerance=±5% resistance=100k power=0.25W package="0603 [SMD]"]
  R9 = Resistor [tolerance=±5% resistance=100k package="0603 [SMD]"]
  R11 = Resistor [tolerance=±5% resistance=1k package="0603 [SMD]"]
  R15 = Resistor [tolerance=±5% resistance=1k package="0603 [SMD]"]
  R14 = Resistor [tolerance=±5% resistance=100k package="0603 [SMD]"]
  R16 = Resistor [tolerance=±5% resistance=1k package="0603 [SMD]"]
  JP8 = female pin header, 4 pins [form="♀ (female)"]
  IC7 = SN74LVC2G14DBVR [part_number=SRV05-4 package=SOT23-6]
  IC8 = SN74LVC2G14DBVR [part_number=SRV05-4 package=SOT23-6]
  IC9 = SN74LVC2G14DBVR [part_number=SRV05-4 package=SOT23-6]
  IC10 = SN74LVC2G14DBVR [part_number=SRV05-4 package=SOT23-6]
  J225 = female pin header, 1 pin [form="♀ (female)"]  # not connected
  J226 = female pin header, 1 pin [form="♀ (female)"]  # not connected
  J227 = female pin header, 1 pin [form="♀ (female)"]  # not connected
  J228 = female pin header, 1 pin [form="♀ (female)"]  # not connected
  J229 = female pin header, 1 pin [form="♀ (female)"]  # not connected
  C32 = Ceramic Capacitor [capacitance=100nF voltage=35V package="0603 [SMD, multilayer]"]
  C33 = Ceramic Capacitor [capacitance=100nF voltage=35V package="0603 [SMD, multilayer]"]
  R25 = Resistor [tolerance=±5% resistance=10 power=2W package="0805 [SMD]"]
  R27 = Resistor [tolerance=±5% resistance=10 power=2W package="0805 [SMD]"]
  R32 = Resistor [tolerance=±5% resistance=10 power=2W package="0805 [SMD]"]
  R31 = Resistor [tolerance=±5% resistance=10 power=1 package="0805 [SMD]"]
  R77 = Resistor [tolerance=±1% resistance=1k power=0.25W package="0603 [SMD]"]
  R78 = Resistor [tolerance=±1% resistance=2.2k power=0.25W package="0603 [SMD]"]
  R63 = Resistor [tolerance=±5% resistance=10k package="0603 [SMD]"]
  C34 = Ceramic Capacitor [capacitance=22µF voltage=6.3V part_number="C59461 " package="0603 [SMD, multilayer]"]
  F1 = Resettable Fuse PTC [part_number=C69680 package=ptc-1206]
  INJ3 = smd LED [color="Red (633nm)" package="0603 [SMD]"]
  D22 = Diode [package=sod-323]
  INJ4 = smd LED [color="Red (633nm)" package="0603 [SMD]"]
  D23 = Diode [package=sod-323]
  INJ2 = smd LED [color="Red (633nm)" package="0603 [SMD]"]
  D21 = Diode [package=sod-323]
  INJ1 = smd LED [color="Red (633nm)" package="0603 [SMD]"]
  D20 = Diode [package=sod-323]
  R82 = Resistor [tolerance=±5% resistance=2.4k power=0.25 package="0603 [SMD]"]
  R83 = Resistor [tolerance=±5% resistance=2.4k power=0.25 package="0603 [SMD]"]
  R81 = Resistor [tolerance=±5% resistance=2.4k power=0.25 package="0603 [SMD]"]
  R80 = Resistor [tolerance=±5% resistance=2.4k power=0.25 package="0603 [SMD]"]

nets:
  O2-CPU-A8/TVS 3: Arduino_Mega_2560.A8, C10.1, R22.Pin_1, IC7.2Y
  A9/TVS 5: Arduino_Mega_2560.A9, C27.1, R64.Pin_1, IC8.1A
  A10/TVS 6: Arduino_Mega_2560.A10, C29.1, R65.Pin_1, IC7.1Y
  IAT-CPU-A0/TVS 9: Arduino_Mega_2560.A0, C2.1, R2.Pin_1, IC9.1Y
  CLT-CPU-A1/TVS 10: Arduino_Mega_2560.A1, C4.1, R4.Pin_1, IC9.1A
  TPS-CPU-A2/TVS 8: Arduino_Mega_2560.A2, C6.1, R6.Pin_1, IC8.2Y
  MAP-CPU-A3/TVS 12: Arduino_Mega_2560.A3, R41.Pin_0, C31.0, IC9.2Y
  BRV-CPU-A4/TVS 7: Arduino_Mega_2560.A4, R8.Pin_1, C8.0, IC8.1Y
  TACH1-CPU-D19/TVS 2: Arduino_Mega_2560.D19/RX1, IC3.pin8, R59.Pin_1, C25.1, IC7.2A
  TACH2-CPU-D18/TVS 1: Arduino_Mega_2560.D18/TX1, IC3.pin7, R60.Pin_1, C24.0, IC7.1A
  STEP-CPU-D17: Arduino_Mega_2560.D17_PWM/RX2, DRV8825.STEP
  STEPDIR-CPU-D16: Arduino_Mega_2560.D16_PWM/TX2, DRV8825.DIRECTION
  GND: Arduino_Mega_2560.GND, Q1.source, Q2.source, Q3.source, Q4.source, U2.P$2, IC3.pin6, Q5.source, Q7.source, Q6.source, Q8.source, C15.0, C13.0, IC6.0V, C16.-, J4.pin9, J4.pin10, J4.pin12, J4.pin23, J3.pin1, IC1.3, IC2.3, MAP.3, DRV8825.GROUND_ST/_MT, DRV8825.GROUND_LOG, C14.-, J110.pin1, J110.pin2, J110.pin3, J110.pin4, J110.pin5, U1.GND, LED1.cathode, LED2.cathode, LED3.cathode, LED4.cathode, AUX_(1_3).pin3, AUX_(1_3).pin4, R35.Pin_0, R37.Pin_0, R36.Pin_0, R38.Pin_0, R21.Pin_1, C7.0, R49.Pin_0, R55.Pin_0, R48.Pin_0, R56.Pin_0, C1.0, C3.0, C5.0, C9.0, C2.0, C4.0, C6.0, C10.0, C8.1, C24.1, C27.0, C29.0, C26.0, C28.0, C25.0, C20.1, C12.0, C11.0, C19.1, C18.1, C31.1, R76.Pin_1, R13.Pin_1, R10.Pin_1, R9.Pin_1, R14.Pin_1, JP8.pin2, IC7.GND, IC8.GND, IC9.GND, IC10.GND, C32.0, C33.0, R78.Pin_1, C34.1
  INJ4-CPU-D11: Arduino_Mega_2560.D11_PWM, R14.Pin_0, R16.Pin_0
  INJ3-CPU-D10: Arduino_Mega_2560.D10_PWM, R13.Pin_0, R15.Pin_0
  INJ2-CPU-D9: Arduino_Mega_2560.D9_PWM, R12.Pin_0, R10.Pin_0
  INJ1-CPU-D8: Arduino_Mega_2560.D8_PWM, R9.Pin_0, R11.Pin_0
  RESET: Arduino_Mega_2560.RESET, R62.Pin_1, C34.0
  5V/MapPwr: Arduino_Mega_2560.5V, IC3.pin5, JP1.pin1, C13.1, MAP.2, DRV8825.RESET, DRV8825.SLEEP, C14.+, U1.output_voltage, R1.Pin_0, R3.Pin_0, R39.Pin_0, R40.Pin_0, R62.Pin_0, R61.Pin_0, C20.0, C19.0, JP8.pin1, IC7.VCC, IC8.VCC, IC9.VCC, IC10.VCC, F1.2
  D0 - RX: Arduino_Mega_2560.D0_RX0, JP8.pin3
  D1 - TX: Arduino_Mega_2560.D1_TX0, R77.Pin_1
  CPU-D2/TVS 13: Arduino_Mega_2560.D2_PWM, R79.Pin_1, IC10.1Y
  CPU-D4: Arduino_Mega_2560.D4_PWM, R58.Pin_0
  CPU-D5: Arduino_Mega_2560.D5_PWM, R50.Pin_0
  CPU-D6: Arduino_Mega_2560.D6_PWM, R57.Pin_0
  CPU-D7: Arduino_Mega_2560.D7_PWM, R51.Pin_0
  CPU-D24: Arduino_Mega_2560.D24, DRV8825.ENABLE
  IGN2-CPU-D24: Arduino_Mega_2560.D38, R24.Pin_0
  LC-CPU-D39: Arduino_Mega_2560.D39, IC6.In_7
  IGN1-CPU-D28: Arduino_Mega_2560.D40, R23.Pin_0
  LC-CPU-D41: Arduino_Mega_2560.D41, IC6.In_6
  LC-CPU-D42: Arduino_Mega_2560.D42
  LC-CPU-D43: Arduino_Mega_2560.D43, IC6.In_2
  LC-CPU-D44: Arduino_Mega_2560.D44
  LC-CPU-D45: Arduino_Mega_2560.D45, IC6.In_4
  LC-CPU-D46: Arduino_Mega_2560.D46
  LC-CPU-D47: Arduino_Mega_2560.D47, IC6.In_1
  LC-CPU-D48: Arduino_Mega_2560.D48
  LC-CPU-D49: Arduino_Mega_2560.D49, IC6.In_3
  IGN4-CPU-D36: Arduino_Mega_2560.D50, R30.Pin_0
  LC-CPU-D51: Arduino_Mega_2560.D51, R75.Pin_1
  IGN3-CPU-D40: Arduino_Mega_2560.D52, R29.Pin_0
  LC-CPU-D53: Arduino_Mega_2560.D53, IC6.In_5
  N1: Q1.gate, R11.Pin_1
  INJ-1-OUT: Q1.drain, J4.pin1, J4.pin40, D20.C
  N2: Q2.gate, R15.Pin_1
  INJ-3-OUT: Q2.drain, J4.pin3, J4.pin4, D22.C
  N3: Q3.gate, R12.Pin_1
  INJ-2-OUT: Q3.drain, J4.pin2, J4.pin39, D21.C
  N4: Q4.gate, R16.Pin_1
  INJ-4-OUT: Q4.drain, J4.pin5, J4.pin6, D23.C
  12V-raw: U2.P$1, JP1.pin3, IC6.COM_-_Common, J3.pin2, D15.A, DRV8825.VOLTAGE_ST/_MT, R7.Pin_0, R63.Pin_1
  VR1-: IC3.pin1, J4.pin27
  N5: IC3.pin2, JP2.pin3
  N6: IC3.pin3, JP3.pin1
  VR2-: IC3.pin4, J4.pin26
  JP1-OUT: JP1.pin2, IC1.6, IC2.6, C12.1, C11.1, C32.1, C33.1
  N7: JP2.pin1, R59.Pin_0
  VR1+: JP2.pin2, JP4.pin2, J4.pin25
  VR2+: JP3.pin2, JP5.pin1, J4.pin24
  N8: JP3.pin3, R60.Pin_0
  N9: JP4.pin1, R39.Pin_1
  N10: JP5.pin2, R40.Pin_1
  N11: Q5.gate, R57.Pin_1, R55.Pin_1
  HC-1-OUT: Q5.drain, J4.pin36
  N12: Q7.gate, R50.Pin_1, R48.Pin_1
  IDLE-OUT: Q7.drain, J4.pin37
  N13: Q6.gate, R58.Pin_1, R56.Pin_1
  HC-2-OUT: Q6.drain, J4.pin38
  N14: Q8.gate, R51.Pin_1, R49.Pin_1
  BOOST-OUT: Q8.drain, J4.pin35
  12V/12V-2: C15.1, C16.+, D15.C, U1.input_voltage, R82.Pin_0, R83.Pin_0, R81.Pin_0, R80.Pin_0
  D39: IC6.Out_7, AUX_(1_3).pin8
  D41: IC6.Out_6, AUX_(1_3).pin7
  D53: IC6.Out_5, AUX_(1_3).pin6
  FuelPump-IDC16: IC6.Out_4, J4.pin16
  TacH-IDC17: IC6.Out_3, J4.pin17, R63.Pin_0
  D43: IC6.Out_2, AUX_(1_3).pin5
  Fan-IDC15: IC6.Out_1, J4.pin15
  IGN-1-OUT: J4.pin7, R67.Pin_1, R27.Pin_0
  IGN-4-OUT: J4.pin8, R68.Pin_1, R32.Pin_1
  MapToECU: J4.pin11, MAP.4, R41.Pin_1, C18.0, R76.Pin_0
  5V-External: J4.pin13, J4.pin28, J109.pin1, J109.pin2, J109.pin3, J109.pin4, J109.pin5, F1.1
  ETH-ICD14: J4.pin14, R79.Pin_0, R61.Pin_1
  Clutch-IDC18: J4.pin18, R75.Pin_0
  CLT Sensor: J4.pin19, R3.Pin_1, C3.1, R4.Pin_0
  IAT Sensor: J4.pin20, R1.Pin_1, C1.1, R2.Pin_0
  O2 Sensor: J4.pin21, C9.1, R22.Pin_0
  TPS Sensor: J4.pin22, C5.1, R6.Pin_0
  STEP-2B-OUT: J4.pin29, DRV8825.OUT_2B
  STEP-2A-OUT: J4.pin30, DRV8825.OUT_2A
  STEP-1A-OUT: J4.pin31, DRV8825.OUT_1A
  STEP-1B-OUT: J4.pin32, DRV8825.OUT_1B
  IGN-3-OUT: J4.pin33, R69.Pin_1, R31.Pin_0
  IGN-2-OUT: J4.pin34, R66.Pin_1, R25.Pin_1
  N15: IC1.2, R23.Pin_1, R37.Pin_1
  N16: IC1.4, R24.Pin_1, R35.Pin_1
  N17: IC1.5, R25.Pin_0
  N18: IC1.7, R27.Pin_1
  N19: IC2.2, R29.Pin_1, R38.Pin_1
  N20: IC2.4, R36.Pin_1, R30.Pin_1
  N21: IC2.5, R32.Pin_0
  N22: IC2.7, R31.Pin_1
  N23: R66.Pin_0, LED1.anode
  N24: R69.Pin_0, LED4.anode
  N25: R68.Pin_0, LED3.anode
  N26: R67.Pin_0, LED2.anode
  A10-OUT: AUX_(1_3).pin1, C28.1, R65.Pin_0
  A9-OUT: AUX_(1_3).pin2, C26.1, R64.Pin_0
  N27: R21.Pin_0, C7.1, R8.Pin_0, R7.Pin_1
  N28: JP8.pin4, R77.Pin_0, R78.Pin_0
  N29: INJ3.cathode, D22.A
  N30: INJ3.anode, R82.Pin_1
  N31: INJ4.cathode, D23.A
  N32: INJ4.anode, R83.Pin_1
  N33: INJ2.cathode, D21.A
  N34: INJ2.anode, R81.Pin_1
  N35: INJ1.cathode, D20.A
  N36: INJ1.anode, R80.Pin_1

notes:
  Injector 1
  Injector 3
  Injector 2
  Injector 4
  Ignition Output IC1
  12v
  5v
  IGN Out
  DetonationEMS.com
  Generic Outputs - High Current
  VR
  Hall
  Reset Protection - Refer AVR040 Application note
  Stepper Driver
  PWM Idle / Boost
  GND
  v1.3
  © 2021 Aaron S.
  Protection
  Ignition Output IC2
  TX RX
  GND VCC
  Flex Input
  Inputs
  TPS Input
  o2 Input
  IAT Input
  Battery Ref
  Coolant Temp
  CMP/CKP
  [ 0-5v Spare Input ]
  Select Board Layout "Speeduino V0.4"
  D43
  [ Spare Outputs ]
  D53
  D41
  D39
  1
  A9 A10
  GND GND
  REV D
  DRV8825
  CHECK INSTALLATION
  DIRECTION!!!!!
  Jumper Config same as Speeduino V0.4
  Aux In/Out
  Bluetooth Header
  ULN2003a
  Map Sensor
  Proto
  Power Supply

custom parts:
  Diode: Diode These are standard reverse protection diodes and small signal diodes. SMA package can handle up to about 1A. SOD-323 can handle about 200mA. What the SOD-323 package when ordering, there are some mfgs out there that are 5-pin packages.
